# Fritzing sketch Untitled Sketch 2 (saved by Fritzing 0.9.9b)

parts:
  Mod1 = Raspberry Pi Pico
  S1 = Pushbutton [package="[THT]"]

nets:
  N1: Mod1.pin_18, S1.Pin_3, S1.Pin_4
  N2: Mod1.pin_21, S1.Pin_1, S1.Pin_2

custom parts:
  Raspberry Pi Pico: Raspberry Pi Pico. Based around the RP2040 microcontroller the Pico is a low cost microcontroller device bringing Raspberry Pi quality, cost, and easy of use to the microcontroller space. Jan 2021, Split part in to two versions: tht (this one) and SMD. This one will drill holes for a .1 in header in pcb to allow plugging in the module as well as providing pads to solder the module to the top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
